# Fritzing sketch acoloid (saved by Fritzing 0.7.12b)
breadboards: 1

parts:
  Arduino1 = Arduino
  U1 = Bluetooth Chipset CSR [part_number=bc417143]
  LED1 = RGB LED (com. cathode, rgb) [package="5 mm [THT]"]
  R1 = Resistor [tolerance=±5% resistance=330 package=THT]

nets:
  N1: Arduino1.GND, U1.GRD, R1.Pin_0
  N2: Arduino1.D10, LED1.red_anode
  N3: Arduino1.D9, LED1.green_anode
  N4: Arduino1.D8, LED1.blue_anode
  N5: Arduino1.D1TX, U1.RX
  N6: Arduino1.D0RX, U1.TX
  +5V: Arduino1.+5V, U1.VCC
  N7: LED1.common_cathode, R1.Pin_1

custom parts:
  Bluetooth Chipset CSR: Bluetooth module uses CSR Bluecore4
